// Logisim project Project MCTE 2332 .circ as structural Verilog: 1 circuit, main circuit main
module main (
  input  total1,
  input  in1,
  input  out1,
  input  total2,
  input  in2,
  input  out2,
  output a1,
  output b1,
  output z,
  output y,
  output a2,
  output b2
);

  LED led_1 (.in(in1));
  LED led_2 (.in(out1));
  LED led_3 (.in(in2));
  LED led_4 (.in(out2));
  Subtractor #(.width(1)) subtractor_1 (.a(total1), .b(in1), .out(a1));  // open: bin, bout
  Adder #(.width(1)) adder_1 (.a(a1), .b(out1), .out(b1));  // open: cin, cout
  Subtractor #(.width(1)) subtractor_2 (.a(total2), .b(in2), .out(a2));  // open: bin, bout
  Adder #(.width(1)) adder_2 (.a(a2), .b(out2), .out(b2));  // open: cin, cout
  Adder #(.width(1)) adder_3 (.a(b1), .b(b2), .out(z), .cout(y));  // open: cin

  // Notes on the sheet:
  //   1913066
endmodule
